// Logisim project ALU.circ as structural Verilog: 1 circuit, main circuit ALU
module ALU (
  input  [7:0] A,
  input  [7:0] B,
  input  Substract,
  output Start,
  output out_5,
  output out_6,
  output out_7,
  output out_8,
  output out_9,
  output out_10,
  output out_11,
  output Overflow
);

  wire adder_1_cout, adder_2_cout, adder_3_cout, adder_4_cout, adder_5_cout, adder_6_cout, adder_7_cout,
       xor_1_out, xor_2_out, xor_3_out, xor_4_out, xor_5_out, xor_6_out, xor_7_out, xor_8_out;

  xor xor_1 (xor_1_out, B[0], Substract);
  xor xor_2 (xor_2_out, B[1], Substract);
  xor xor_3 (xor_3_out, B[2], Substract);
  xor xor_4 (xor_4_out, B[3], Substract);
  xor xor_5 (xor_5_out, B[4], Substract);
  xor xor_6 (xor_6_out, B[5], Substract);
  xor xor_7 (xor_7_out, B[6], Substract);
  xor xor_8 (xor_8_out, B[7], Substract);
  Adder #(.width(1)) adder_1 (.a(A[0]), .b(xor_1_out), .out(Start), .cin(Substract), .cout(adder_1_cout));
  Adder #(.width(1)) adder_2 (.a(A[1]), .b(xor_2_out), .out(out_5), .cin(adder_1_cout), .cout(adder_2_cout));
  Adder #(.width(1)) adder_3 (.a(A[2]), .b(xor_3_out), .out(out_6), .cin(adder_2_cout), .cout(adder_3_cout));
  Adder #(.width(1)) adder_4 (.a(A[3]), .b(xor_4_out), .out(out_7), .cin(adder_3_cout), .cout(adder_4_cout));
  Adder #(.width(1)) adder_5 (.a(A[4]), .b(xor_5_out), .out(out_8), .cin(adder_4_cout), .cout(adder_5_cout));
  Adder #(.width(1)) adder_6 (.a(A[5]), .b(xor_6_out), .out(out_9), .cin(adder_5_cout), .cout(adder_6_cout));
  Adder #(.width(1)) adder_7 (.a(A[6]), .b(xor_7_out), .out(out_10), .cin(adder_6_cout), .cout(adder_7_cout));
  Adder #(.width(1)) adder_8 (.a(A[7]), .b(xor_8_out), .out(out_11), .cin(adder_7_cout), .cout(Overflow));
endmodule
